# Fritzing sketch SpratSensorControl (saved by Fritzing 0.8.7b)
breadboards: 1

parts:
  EtherMega = Arduino Mega ADK (Rev3)
  DHT22-1 = Humidity and Temperature Sensor RHT03
  DHT22-2 = Humidity and Temperature Sensor RHT03
  MPU-1 = SparkFun MPU-6050 Board [form="♀ (female)" package=THT]

nets:
  N1: EtherMega.D21/SCL, MPU-1.pin5
  N2: EtherMega.D20/SDA, MPU-1.pin6
  N3: EtherMega.GND, DHT22-1.GND_1, DHT22-1.GND_2, DHT22-2.GND_1, DHT22-2.GND_2, MPU-1.pin2
  N4: EtherMega.3V3, MPU-1.pin1
  N5: EtherMega.D6_PWM, DHT22-1.Data-signal
  N6: EtherMega.D7_PWM, DHT22-2.Data-signal
  VCC: DHT22-1.Vcc, DHT22-2.Vcc

custom parts:
  SparkFun MPU-6050 Board: SparkFUN MPU-6050 Board
